// Logisim project mesm_6.circ as structural Verilog: 12 circuits, main circuit main
module main (
);

  wire clock_1_out, cpu_1_dbus_read, cpu_1_dbus_write, cpu_1_ibus_fetch, dram_1_dbus_done, irom_1_o_done,
       IRQ_out, RESET_out;
  wire [14:0] cpu_1_dbus_addr, cpu_1_ibus_addr;
  wire [23:0] cpu_1_dbus_odata_h, cpu_1_dbus_odata_l, dram_1_dbus_odata_h, dram_1_dbus_odata_l,
       irom_1_odata_h, irom_1_odata_l;

  Clock clock_1 (.out(clock_1_out));
  Button RESET (.out(RESET_out));
  Button IRQ (.out(IRQ_out));
  IROM irom_1 (
    .CLK(clock_1_out), .FETCH(cpu_1_ibus_fetch), .I_ADDR(cpu_1_ibus_addr), .ODATA_L(irom_1_odata_l),
    .ODATA_H(irom_1_odata_h), .O_DONE(irom_1_o_done));
  CPU cpu_1 (
    .CLK(clock_1_out), .RESET(RESET_out), .IRQ(IRQ_out), .IBUS_IDATA_L(irom_1_odata_l),
    .IBUS_IDATA_H(irom_1_odata_h), .IBUS_DONE(irom_1_o_done), .DBUS_IDATA_L(dram_1_dbus_odata_l),
    .DBUS_IDATA_H(dram_1_dbus_odata_h), .DBUS_DONE(dram_1_dbus_done), .IBUS_FETCH(cpu_1_ibus_fetch),
    .IBUS_ADDR(cpu_1_ibus_addr), .DBUS_READ(cpu_1_dbus_read), .DBUS_WRITE(cpu_1_dbus_write),
    .DBUS_ADDR(cpu_1_dbus_addr), .DBUS_ODATA_L(cpu_1_dbus_odata_l), .DBUS_ODATA_H(cpu_1_dbus_odata_h));
  DRAM dram_1 (
    .CLK(clock_1_out), .DBUS_READ(cpu_1_dbus_read), .DBUS_WRITE(cpu_1_dbus_write),
    .DBUS_ADDR(cpu_1_dbus_addr), .DBUS_IDATA_L(cpu_1_dbus_odata_l), .DBUS_IDATA_H(cpu_1_dbus_odata_h),
    .DBUS_DONE(dram_1_dbus_done), .DBUS_ODATA_L(dram_1_dbus_odata_l), .DBUS_ODATA_H(dram_1_dbus_odata_h));
endmodule

module CU (
  input  CLK,
  input  RESET,
  input  IRQ,
  input  BUSY,
  input  in_5,
  input  [23:0] cmd,
  output [2:0] sel_acc,
  output [2:0] sel_md,
  output [1:0] sel_mw,
  output w_m,
  output [1:0] sel_mr,
  output m_use,
  output [2:0] sel_pc,
  output sel_addr,
  output sel_j_addr,
  output w_a,
  output w_c,
  output w_y,
  output a_neg,
  output a_zero,
  output clear_c,
  output enter_int,
  output exit_int,
  output w_pc
);

  wire branch, decode, undriven_2;
  wire [8:0] adder_1_out, imm, multiplexer_1_out, multiplexer_2_out, multiplexer_3_out, multiplexer_4_out,
       reset_vector, undriven, upc_q;

  Adder #(.width(9)) adder_1 (.a(9'h1), .b(upc_q), .out(adder_1_out));  // open: cin, cout
  Multiplexer #(.width(9), .enable("false")) multiplexer_1 (
    .in0(adder_1_out), .in1(undriven), .out(multiplexer_1_out), .sel(decode));
  Multiplexer #(.width(9), .enable("false")) multiplexer_2 (
    .in0(multiplexer_1_out), .in1(imm), .out(multiplexer_2_out), .sel(branch));
  Multiplexer #(.width(9), .enable("false")) multiplexer_3 (
    .in0(multiplexer_2_out), .in1(upc_q), .out(multiplexer_3_out), .sel(BUSY));
  Multiplexer #(.width(9), .enable("false")) multiplexer_4 (
    .in0(multiplexer_3_out), .in1(reset_vector), .out(multiplexer_4_out), .sel(RESET));
  Register #(.width(9)) upc (.D(multiplexer_4_out), .en(1'b1), .clk(CLK), .Q(upc_q), .clr(1'b0));
  // Probe on undriven_2

  // Other names for the same wires on the sheet: uop_h (some bits) = {w_pc, exit_int, enter_int, clear_c, branch, a_zero, a_neg, w_y, w_c, w_a, decode};
  //   uop_l (some bits) = {sel_j_addr, sel_addr, sel_pc, m_use, sel_mr, w_m, sel_mw, sel_md, sel_acc, imm}
endmodule

module PC_reg (
  input  clk,
  input  w_pc,
  input  [15:0] U_addr,
  input  [15:0] V_addr,
  input  [15:0] M_i,
  input  [15:0] imm,
  output [15:0] pc_q
);

  wire [15:0] adder_1_out, multiplexer_1_out;

  // Probe on adder_1_out
  Multiplexer #(.select(3), .width(16), .enable("false")) multiplexer_1 (
    .in0(U_addr), .in1(V_addr), .in2(M_i), .in3(imm), .in4(adder_1_out), .out(multiplexer_1_out));  // open: in5, in6, in7, sel
  Register #(.width(16)) PC (.D(multiplexer_1_out), .en(w_pc), .clk(clk), .Q(pc_q), .clr(1'b0));
  Adder #(.width(16)) adder_1 (.a(pc_q), .b(16'h1), .out(adder_1_out));  // open: cin, cout
endmodule

module C_reg (
  input  sel_c,
  input  [14:0] U_addr,
  input  [14:0] dbus_out,
  input  w_c,
  input  clk,
  output [14:0] C_q
);

  wire [14:0] multiplexer_1_out;

  Multiplexer #(.width(15), .enable("false")) multiplexer_1 (
    .in0(U_addr), .in1(dbus_out), .out(multiplexer_1_out), .sel(sel_c));
  Register #(.width(15)) C_reg (.D(multiplexer_1_out), .en(w_c), .clk(clk), .Q(C_q), .clr(1'b0));
endmodule

module U_addr_gen (
  input  clk,
  input  sel_j_add,
  input  c_active,
  input  [23:0] cmd,
  input  [14:0] C_in,
  input  decode,
  input  [14:0] M_j,
  input  [14:0] M_i,
  output [14:0] U_addr
);

  wire [14:0] adder_1_out, bit_extender_1_out, multiplexer_1_out, multiplexer_2_out, multiplexer_3_out,
       V_ADDR_q;

  assign bit_extender_1_out = {{2{cmd[18]}}, {cmd[18], cmd[11:0]}};  // Bit_Extender bit_extender_1
  Multiplexer #(.width(15), .enable("false")) multiplexer_1 (
    .in0(bit_extender_1_out), .in1(cmd[14:0]), .out(multiplexer_1_out), .sel(cmd[19]));
  Adder #(.width(15)) adder_1 (.a(multiplexer_1_out), .b(C_in), .out(adder_1_out));  // open: cin, cout
  Multiplexer #(.width(15), .enable("false")) multiplexer_2 (
    .in0(multiplexer_1_out), .in1(adder_1_out), .out(multiplexer_2_out), .sel(c_active));
  Register #(.width(15)) V_ADDR (.D(multiplexer_2_out), .en(decode), .clk(clk), .Q(V_ADDR_q), .clr(1'b0));
  Multiplexer #(.width(15), .enable("false")) multiplexer_3 (
    .in0(V_ADDR_q), .in1(M_j), .out(multiplexer_3_out), .sel(sel_j_add));
  Adder #(.width(15)) adder_2 (.a(multiplexer_3_out), .b(M_i), .out(U_addr));  // open: cin, cout

  // Notes on the sheet:
  //   op_addr
  //   C + op_addr
endmodule

module M_regs (
  input  clk,
  input  [1:0] sel_mr,
  input  [3:0] reg_ind,
  input  [3:0] imm,
  input  [14:0] V_addr,
  input  [14:0] U_addr,
  input  [1:0] sel_mw,
  input  w_m,
  input  [2:0] sel_md,
  input  [14:0] PC,
  input  [14:0] ACC,
  input  [14:0] M_i,
  input  [14:0] M_i_p1,
  input  [14:0] M_i_m1,
  output [14:0] RD1,
  output [14:0] RD2
);

  wire decoder_1_out1, decoder_1_out2, decoder_1_out3, decoder_1_out4, decoder_1_out5, decoder_1_out6,
       decoder_1_out7, decoder_1_out8, decoder_1_out9, decoder_1_out10, decoder_1_out11, decoder_1_out12,
       decoder_1_out13, decoder_1_out14, decoder_1_out15, decoder_2_out1, decoder_2_out2, decoder_2_out3,
       decoder_2_out4, decoder_2_out5, decoder_2_out6, decoder_2_out7, decoder_2_out8, decoder_2_out9,
       decoder_2_out10, decoder_2_out11, decoder_2_out12, decoder_2_out13, decoder_2_out14, decoder_2_out15,
       decoder_3_out1, decoder_3_out2, decoder_3_out3, decoder_3_out4, decoder_3_out5, decoder_3_out6,
       decoder_3_out7, decoder_3_out8, decoder_3_out9, decoder_3_out10, decoder_3_out11, decoder_3_out12,
       decoder_3_out13, decoder_3_out14, decoder_3_out15;
  wire [3:0] bit_extender_1_out, bit_extender_2_out, multiplexer_1_out, multiplexer_2_out;
  wire [14:0] M1_q, M2_q, M3_q, M4_q, M5_q, M6_q, M7_q, M8_q, M9_q, M10_q, M11_q, M12_q, M13_q, M14_q, M15_q,
       multiplexer_3_out;

  Bit_Extender #(.in_width(15), .out_width(4), .\type ("zero")) bit_extender_1 (.in(V_addr), .out(bit_extender_1_out));
  Bit_Extender #(.in_width(15), .out_width(4), .\type ("zero")) bit_extender_2 (.in(U_addr), .out(bit_extender_2_out));
  Multiplexer #(.select(2), .width(4)) multiplexer_1 (
    .in0(reg_ind), .in1(imm), .in2(bit_extender_1_out), .in3(bit_extender_2_out), .out(multiplexer_1_out),
    .sel(sel_mw), .en(w_m));
  Multiplexer #(.select(2), .width(4), .enable("false")) multiplexer_2 (
    .in0(reg_ind), .in1(imm), .in2(bit_extender_1_out), .in3(bit_extender_2_out), .out(multiplexer_2_out),
    .sel(sel_mr));
  Multiplexer #(.select(3), .width(15), .enable("false")) multiplexer_3 (
    .in0(PC), .in1(ACC), .in2(M_i), .in3(M_i_p1), .in4(M_i_m1), .in5(V_addr), .in6(U_addr),
    .out(multiplexer_3_out), .sel(sel_md));  // open: in7
  Decoder #(.select(4), .enable("false")) decoder_1 (
    .out1(decoder_1_out1), .out2(decoder_1_out2), .out3(decoder_1_out3), .out4(decoder_1_out4),
    .out5(decoder_1_out5), .out6(decoder_1_out6), .out7(decoder_1_out7), .out8(decoder_1_out8),
    .out9(decoder_1_out9), .out10(decoder_1_out10), .out11(decoder_1_out11), .out12(decoder_1_out12),
    .out13(decoder_1_out13), .out14(decoder_1_out14), .out15(decoder_1_out15), .sel(multiplexer_1_out));  // open: out0
  Register #(.width(15)) M1 (.D(multiplexer_3_out), .en(decoder_1_out1), .clk(clk), .Q(M1_q), .clr(1'b0));
  Register #(.width(15)) M2 (.D(multiplexer_3_out), .en(decoder_1_out2), .clk(clk), .Q(M2_q), .clr(1'b0));
  Register #(.width(15)) M3 (.D(multiplexer_3_out), .en(decoder_1_out3), .clk(clk), .Q(M3_q), .clr(1'b0));
  Register #(.width(15)) M4 (.D(multiplexer_3_out), .en(decoder_1_out4), .clk(clk), .Q(M4_q), .clr(1'b0));
  assign RD1 = decoder_2_out1 ? M1_q : 15'bz;  // Controlled_Buffer controlled_buffer_1
  assign RD2 = decoder_3_out1 ? M1_q : 15'bz;  // Controlled_Buffer controlled_buffer_2
  Decoder #(.select(4), .enable("false")) decoder_2 (
    .out1(decoder_2_out1), .out2(decoder_2_out2), .out3(decoder_2_out3), .out4(decoder_2_out4),
    .out5(decoder_2_out5), .out6(decoder_2_out6), .out7(decoder_2_out7), .out8(decoder_2_out8),
    .out9(decoder_2_out9), .out10(decoder_2_out10), .out11(decoder_2_out11), .out12(decoder_2_out12),
    .out13(decoder_2_out13), .out14(decoder_2_out14), .out15(decoder_2_out15), .sel(multiplexer_2_out));  // open: out0
  assign RD1 = decoder_2_out2 ? M2_q : 15'bz;  // Controlled_Buffer controlled_buffer_3
  assign RD2 = decoder_3_out2 ? M2_q : 15'bz;  // Controlled_Buffer controlled_buffer_4
  assign RD1 = decoder_2_out3 ? M3_q : 15'bz;  // Controlled_Buffer controlled_buffer_5
  assign RD2 = decoder_3_out3 ? M3_q : 15'bz;  // Controlled_Buffer controlled_buffer_6
  assign RD1 = decoder_2_out4 ? M4_q : 15'bz;  // Controlled_Buffer controlled_buffer_7
  assign RD2 = decoder_3_out4 ? M4_q : 15'bz;  // Controlled_Buffer controlled_buffer_8
  Decoder #(.select(4), .enable("false")) decoder_3 (
    .out1(decoder_3_out1), .out2(decoder_3_out2), .out3(decoder_3_out3), .out4(decoder_3_out4),
    .out5(decoder_3_out5), .out6(decoder_3_out6), .out7(decoder_3_out7), .out8(decoder_3_out8),
    .out9(decoder_3_out9), .out10(decoder_3_out10), .out11(decoder_3_out11), .out12(decoder_3_out12),
    .out13(decoder_3_out13), .out14(decoder_3_out14), .out15(decoder_3_out15), .sel(bit_extender_1_out));  // open: out0
  Register #(.width(15)) M5 (.D(multiplexer_3_out), .en(decoder_1_out5), .clk(clk), .Q(M5_q), .clr(1'b0));
  Register #(.width(15)) M6 (.D(multiplexer_3_out), .en(decoder_1_out6), .clk(clk), .Q(M6_q), .clr(1'b0));
  Register #(.width(15)) M7 (.D(multiplexer_3_out), .en(decoder_1_out7), .clk(clk), .Q(M7_q), .clr(1'b0));
  Register #(.width(15)) M8 (.D(multiplexer_3_out), .en(decoder_1_out8), .clk(clk), .Q(M8_q), .clr(1'b0));
  assign RD1 = decoder_2_out5 ? M5_q : 15'bz;  // Controlled_Buffer controlled_buffer_9
  assign RD2 = decoder_3_out5 ? M5_q : 15'bz;  // Controlled_Buffer controlled_buffer_10
  assign RD1 = decoder_2_out6 ? M6_q : 15'bz;  // Controlled_Buffer controlled_buffer_11
  assign RD2 = decoder_3_out6 ? M6_q : 15'bz;  // Controlled_Buffer controlled_buffer_12
  assign RD1 = decoder_2_out7 ? M7_q : 15'bz;  // Controlled_Buffer controlled_buffer_13
  assign RD2 = decoder_3_out7 ? M7_q : 15'bz;  // Controlled_Buffer controlled_buffer_14
  assign RD1 = decoder_2_out8 ? M8_q : 15'bz;  // Controlled_Buffer controlled_buffer_15
  assign RD2 = decoder_3_out8 ? M8_q : 15'bz;  // Controlled_Buffer controlled_buffer_16
  Register #(.width(15)) M9 (.D(multiplexer_3_out), .en(decoder_1_out9), .clk(clk), .Q(M9_q), .clr(1'b0));
  Register #(.width(15)) M10 (.D(multiplexer_3_out), .en(decoder_1_out10), .clk(clk), .Q(M10_q), .clr(1'b0));
  Register #(.width(15)) M11 (.D(multiplexer_3_out), .en(decoder_1_out11), .clk(clk), .Q(M11_q), .clr(1'b0));
  Register #(.width(15)) M12 (.D(multiplexer_3_out), .en(decoder_1_out12), .clk(clk), .Q(M12_q), .clr(1'b0));
  assign RD1 = decoder_2_out9 ? M9_q : 15'bz;  // Controlled_Buffer controlled_buffer_17
  assign RD2 = decoder_3_out9 ? M9_q : 15'bz;  // Controlled_Buffer controlled_buffer_18
  assign RD1 = decoder_2_out10 ? M10_q : 15'bz;  // Controlled_Buffer controlled_buffer_19
  assign RD2 = decoder_3_out10 ? M10_q : 15'bz;  // Controlled_Buffer controlled_buffer_20
  assign RD1 = decoder_2_out11 ? M11_q : 15'bz;  // Controlled_Buffer controlled_buffer_21
  assign RD2 = decoder_3_out11 ? M11_q : 15'bz;  // Controlled_Buffer controlled_buffer_22
  assign RD1 = decoder_2_out12 ? M12_q : 15'bz;  // Controlled_Buffer controlled_buffer_23
  assign RD2 = decoder_3_out12 ? M12_q : 15'bz;  // Controlled_Buffer controlled_buffer_24
  Register #(.width(15)) M13 (.D(multiplexer_3_out), .en(decoder_1_out13), .clk(clk), .Q(M13_q), .clr(1'b0));
  Register #(.width(15)) M14 (.D(multiplexer_3_out), .en(decoder_1_out14), .clk(clk), .Q(M14_q), .clr(1'b0));
  Register #(.width(15)) M15 (.D(multiplexer_3_out), .en(decoder_1_out15), .clk(clk), .Q(M15_q), .clr(1'b0));
  assign RD1 = decoder_2_out13 ? M13_q : 15'bz;  // Controlled_Buffer controlled_buffer_25
  assign RD2 = decoder_3_out13 ? M13_q : 15'bz;  // Controlled_Buffer controlled_buffer_26
  assign RD1 = decoder_2_out14 ? M14_q : 15'bz;  // Controlled_Buffer controlled_buffer_27
  assign RD2 = decoder_3_out14 ? M14_q : 15'bz;  // Controlled_Buffer controlled_buffer_28
  assign RD1 = decoder_2_out15 ? M15_q : 15'bz;  // Controlled_Buffer controlled_buffer_29
  assign RD2 = decoder_3_out15 ? M15_q : 15'bz;  // Controlled_Buffer controlled_buffer_30

  // Notes on the sheet:
  //   RA1
  //   RA2
  //   WA
endmodule

module ALU (
  input  CLK,
  input  [23:0] ALU_A_H,
  input  [23:0] ALU_A_L,
  input  [23:0] ALU_B_H,
  input  [23:0] ALU_B_L,
  input  [5:0] ALU_OP,
  output [23:0] ALU_R_H,
  output [23:0] ALU_R_L,
  output [23:0] ALU_Y_H,
  output [23:0] ALU_Y_L,
  output ALU_DONE
);


  assign ALU_DONE = 1'b0;
endmodule

module IROM (
  input  CLK,
  input  FETCH,
  input  [14:0] I_ADDR,
  output [23:0] ODATA_L,
  output [23:0] ODATA_H,
  output O_DONE
);

  wire and_1_out, not_1_out;
  wire [23:0] IROM_H_data, IROM_L_data;

  ROM #(.addrWidth(15), .dataWidth(24)) IROM_L (.addr(I_ADDR), .data(IROM_L_data));
  Register #(.width(1)) register_1 (.D(FETCH), .en(1'b1), .clk(CLK), .Q(O_DONE), .clr(1'b0));
  not not_1 (not_1_out, O_DONE);
  and and_1 (and_1_out, FETCH, not_1_out);
  Register #(.width(24)) register_2 (.D(IROM_L_data), .en(and_1_out), .clk(CLK), .Q(ODATA_L), .clr(1'b0));
  ROM #(.addrWidth(15), .dataWidth(24)) IROM_H (.addr(I_ADDR), .data(IROM_H_data));
  Register #(.width(24)) register_3 (.D(IROM_H_data), .en(and_1_out), .clk(CLK), .Q(ODATA_H), .clr(1'b0));
endmodule

module CPU (
  input  CLK,
  input  RESET,
  input  IRQ,
  input  [23:0] IBUS_IDATA_L,
  input  [23:0] IBUS_IDATA_H,
  input  IBUS_DONE,
  input  [23:0] DBUS_IDATA_L,
  input  [23:0] DBUS_IDATA_H,
  input  DBUS_DONE,
  output IBUS_FETCH,
  output [14:0] IBUS_ADDR,
  output DBUS_READ,
  output DBUS_WRITE,
  output [14:0] DBUS_ADDR,
  output [23:0] DBUS_ODATA_L,
  output [23:0] DBUS_ODATA_H
);

  wire ACC_IS_NEG, ACC_IS_ZERO, alu_done, and_2_out, and_3_out, and_4_out, and_5_out, and_6_out, and_7_out,
       and_8_out, and_9_out, branch, busy, comparator_1_eq, comparator_2_eq, comparator_3_eq, cond_acc_neg,
       cond_acc_nonzero, cond_acc_zero, cond_op_not_cached, dbus_read_t, dbus_write_t, decode, fetch,
       IS_OP_CACHED, Mi_is_zero, not_1_out, not_2_out, not_3_out, not_4_out, not_5_out, not_6_out, not_7_out,
       not_8_out, or_1_out, P_C_ACTIVE, P_DECODE, P_ENTER_INT, P_EXIT_INT, P_M_ZERO, P_SEL_ALU_MEM, P_W_A,
       P_W_C, P_W_PC, sel_c_mem, w_opcode;
  wire [5:0] alu_op;
  wire [8:0] adder_1_out, imm, jmp_tbl_1_mc_addr, multiplexer_1_out, multiplexer_2_out, multiplexer_3_out,
       multiplexer_4_out, upc_next, UPC_q;
  wire [14:0] PC_CACHED_q;
  wire [15:0] PC_Q;
  wire [23:0] ACC_H_q, ACC_L_q, OPCODE_CACHE_H_q, OPCODE_CACHE_L_q;
  wire [31:3] uop_h;
  wire [31:15] uop_l;

  or or_1 (or_1_out, dbus_read_t, dbus_write_t);
  not not_1 (not_1_out, DBUS_DONE);
  not not_2 (not_2_out, IBUS_DONE);
  Comparator #(.width(6)) comparator_1 (.a(alu_op), .b({6{1'b0}}), .eq(comparator_1_eq));  // open: gt, lt
  not not_3 (not_3_out, alu_done);
  not not_4 (not_4_out, busy);
  and and_1 (decode, not_4_out, P_DECODE);
  and and_2 (and_2_out, cond_op_not_cached, not_5_out);
  not not_5 (not_5_out, IS_OP_CACHED);
  and and_3 (and_3_out, cond_acc_zero, ACC_IS_ZERO);
  not not_6 (not_6_out, ACC_IS_ZERO);
  and and_4 (and_4_out, not_6_out, cond_acc_nonzero);
  and and_5 (and_5_out, cond_acc_neg, ACC_IS_NEG);
  and and_6 (and_6_out, P_M_ZERO, Mi_is_zero);
  and and_7 (and_7_out, or_1_out, not_1_out);
  and and_8 (and_8_out, fetch, not_2_out);
  not not_7 (not_7_out, comparator_1_eq);
  and and_9 (and_9_out, not_7_out, not_3_out);
  Register #(.width(24)) ACC_L (.Q(ACC_L_q));  // open: D, en, clk, clr
  Register #(.width(24)) ACC_H (.Q({ACC_H_q[23:9], ACC_IS_NEG, ACC_H_q[7:0]}));  // open: D, en, clk, clr
  or or_2 (busy, and_7_out, and_8_out, and_9_out);
  or or_3 (branch, and_2_out, and_3_out, and_4_out, and_5_out, and_6_out, cond_op_not_cached);
  Register #(.width(16)) PC (.Q(PC_Q));  // open: D, en, clk, clr
  Comparator #(.width(24)) comparator_2 (.a(ACC_L_q), .b({24{1'b0}}), .eq(comparator_2_eq));  // open: gt, lt
  Comparator #(.width(24)) comparator_3 (
    .a({ACC_H_q[23:9], ACC_IS_NEG, ACC_H_q[7:0]}), .b({24{1'b0}}), .eq(comparator_3_eq));  // open: gt, lt
  and and_10 (ACC_IS_ZERO, comparator_2_eq, comparator_3_eq);
  JMP_TBL jmp_tbl_1 (.MC_ADDR(jmp_tbl_1_mc_addr));  // open: CMD
  Adder #(.width(9)) adder_1 (.a(9'h1), .b(UPC_q), .out(adder_1_out));  // open: cin, cout
  Multiplexer #(.width(9), .enable("false")) multiplexer_1 (
    .in0(jmp_tbl_1_mc_addr), .in1(9'h17), .out(multiplexer_1_out), .sel(IRQ));
  ALU alu_1 (
    .CLK(CLK), .ALU_OP(alu_op), .ALU_DONE(alu_done));  // open: ALU_A_H, ALU_A_L, ALU_B_H, ALU_B_L, ALU_R_H, ALU_R_L, ALU_Y_H, ALU_Y_L
  Multiplexer #(.width(9), .enable("false")) multiplexer_2 (
    .in0(adder_1_out), .in1(multiplexer_1_out), .out(multiplexer_2_out), .sel(decode));
  Multiplexer #(.width(9), .enable("false")) multiplexer_3 (
    .in0(multiplexer_2_out), .in1(imm), .out(multiplexer_3_out), .sel(branch));
  Multiplexer #(.width(9), .enable("false")) multiplexer_4 (
    .in0(multiplexer_3_out), .in1(UPC_q), .out(multiplexer_4_out), .sel(busy));
  // Probe on upc_next
  Multiplexer #(.width(9), .enable("false")) multiplexer_5 (
    .in0(multiplexer_4_out), .in1({9{1'b0}}), .out(upc_next), .sel(RESET));
  Register #(.width(24)) OPCODE_CACHE_L (
    .D(IBUS_IDATA_L), .en(w_opcode), .clk(CLK), .Q(OPCODE_CACHE_L_q));  // open: clr
  Register #(.width(24)) OPCODE_CACHE_H (
    .D(IBUS_IDATA_H), .en(w_opcode), .clk(CLK), .Q(OPCODE_CACHE_H_q));  // open: clr
  Register #(.width(15)) PC_CACHED (.D(PC_Q[15:1]), .en(w_opcode), .clk(CLK), .Q(PC_CACHED_q));  // open: clr
  Register #(.width(9)) UPC (.D(upc_next), .en(1'b1), .clk(CLK), .Q(UPC_q), .clr(1'b0));
  Comparator #(.width(15)) comparator_4 (.a(PC_CACHED_q), .b(PC_Q[15:1]), .eq(IS_OP_CACHED));  // open: gt, lt
  MC_ROM mc_rom_1 (
    .ADDR(upc_next), .UOP_L({uop_l, alu_op, imm}),
    .UOP_H({uop_h[31:19], P_SEL_ALU_MEM, P_M_ZERO, P_W_PC, P_EXIT_INT, P_ENTER_INT, P_C_ACTIVE, cond_op_not_cached, cond_acc_zero, cond_acc_neg, cond_acc_nonzero, P_W_C, P_W_A, dbus_write_t, dbus_read_t, P_DECODE, uop_h[3], fetch, cond_op_not_cached, sel_c_mem}));
  not not_8 (not_8_out, busy);
  and and_11 (w_opcode, not_8_out, uop_h[3]);

  // Other names for the same wires on the sheet: uop_h (some bits) = {P_SEL_ALU_MEM, P_M_ZERO, P_W_PC, P_EXIT_INT, P_ENTER_INT, P_C_ACTIVE, cond_op_not_cached, cond_acc_zero, cond_acc_neg, cond_acc_nonzero, P_W_C, P_W_A, dbus_write_t, dbus_read_t, P_DECODE, fetch, cond_op_not_cached, sel_c_mem};
  //   ibus_fetch_t = fetch; mem_r = dbus_read_t; mem_w = dbus_write_t; P_A_NONZERO = cond_acc_nonzero;
  //   P_A_ZERO = cond_acc_zero; op_not_cached = cond_op_not_cached; P_BRANCH = cond_op_not_cached;
  //   uop_l[14:0] = {alu_op, imm}

  // Notes on the sheet:
  //   TODO
endmodule

module DRAM (
  input  CLK,
  input  DBUS_READ,
  input  DBUS_WRITE,
  input  [14:0] DBUS_ADDR,
  input  [23:0] DBUS_IDATA_L,
  input  [23:0] DBUS_IDATA_H,
  output DBUS_DONE,
  output [23:0] DBUS_ODATA_L,
  output [23:0] DBUS_ODATA_H
);

  wire comparator_1_eq, comparator_2_eq, or_1_out;
  wire [23:0] multiplexer_1_out, multiplexer_2_out, ram_1_dout, ram_2_dout;

  RAM #(.addrWidth(15), .dataWidth(24), .databus("bibus")) ram_1 (
    .addr(DBUS_ADDR), .we(DBUS_WRITE), .oe(DBUS_READ), .clk(CLK), .din(DBUS_IDATA_L), .dout(ram_1_dout));
  RAM #(.addrWidth(15), .dataWidth(24), .databus("bibus")) ram_2 (
    .addr(DBUS_ADDR), .we(DBUS_WRITE), .oe(DBUS_READ), .clk(CLK), .din(DBUS_IDATA_H), .dout(ram_2_dout));
  Comparator #(.width(15)) comparator_1 (.a(DBUS_ADDR), .b({15{1'b0}}), .eq(comparator_1_eq));  // open: gt, lt
  Comparator #(.width(15)) comparator_2 (.a(DBUS_ADDR), .b({15{1'b0}}), .eq(comparator_2_eq));  // open: gt, lt
  Multiplexer #(.width(24), .enable("false")) multiplexer_1 (
    .in0(ram_1_dout), .in1({24{1'b0}}), .out(multiplexer_1_out), .sel(comparator_1_eq));
  Multiplexer #(.width(24), .enable("false")) multiplexer_2 (
    .in0(ram_2_dout), .in1({24{1'b0}}), .out(multiplexer_2_out), .sel(comparator_2_eq));
  Register #(.width(24)) register_1 (.D(multiplexer_1_out), .en(DBUS_READ), .clk(CLK), .Q(DBUS_ODATA_L), .clr(1'b0));
  Register #(.width(1)) register_2 (.D(or_1_out), .en(1'b1), .clk(CLK), .Q(DBUS_DONE), .clr(1'b0));
  or or_1 (or_1_out, DBUS_WRITE, DBUS_READ);
  Register #(.width(24)) register_3 (.D(multiplexer_2_out), .en(DBUS_READ), .clk(CLK), .Q(DBUS_ODATA_H), .clr(1'b0));
endmodule

module JMP_TBL (
  input  [23:0] CMD,
  output [8:0] MC_ADDR
);

  wire [8:0] rom_1_data, rom_2_data;

  ROM #(.addrWidth(6), .dataWidth(9)) rom_1 (.addr(CMD[17:12]), .data(rom_1_data));
  ROM #(.addrWidth(4), .dataWidth(9)) rom_2 (.addr(CMD[18:15]), .data(rom_2_data));
  Multiplexer #(.width(9), .enable("false")) multiplexer_1 (
    .in0(rom_1_data), .in1(rom_2_data), .out(MC_ADDR), .sel(CMD[19]));

  // Notes on the sheet:
  //   contents of rom_1 (hex, n*v repeats v):
  //   19 1b 1c 1d 1e 1f 20 21 22 24 27 2a 2d 2e 31 32 33 34 35 36 37 38 39 3a 3b 3c 3d 3e 3f 40 41 42 43
  //   45 46 48 49 4a 4b 4c 4d 4e 4f 50 51 52 53 54 55 56 57 58 59 5a 5b 5c 5d 5e 5f 60 61 62 63 64
  //   contents of rom_2 (hex, n*v repeats v):
  //   65 66 67 69 6b 6c 6d 71 75 77 79 7a 7b 7f 83 84
endmodule

module MC_ROM (
  input  [8:0] ADDR,
  output [31:0] UOP_L,
  output [31:0] UOP_H
);

  ROM #(.addrWidth(9), .dataWidth(32)) MC_L (.addr(ADDR), .data(UOP_L));
  ROM #(.addrWidth(9), .dataWidth(32)) MC_H (.addr(ADDR), .data(UOP_H));

  // Notes on the sheet:
  //   contents of MC_L (hex, n*v repeats v):
  //   a40000 1010000 a40001 a40002 a40003 a40004 a40005 a40006 a40007 a40008 a40009 a4000a a4000b a4000c
  //   a4000d a4000e a4000f 18000001 4*0 12 0 12 0 8*12 8000 12 8000 200 12 8000 600 12 8000 a00 12 12 8000
  //   400 19*12 e40012 12 12 3010000 12 12 c80012 82d80012 28*12 0 14 0 14 940012 980012 6f 12 0 12 73 12
  //   0 12 0 12 8800000 12 12 12 7d 12 8000000 12 4000081 12 8000000 12 12 4000086 12 88c0000 12
  //   contents of MC_H (hex, n*v repeats v):
  //   0 80 15*0 18000 c 10 c 2010 12 4000 12 40 8*12 a0 12 20 40080 12 20 40080 12 20 40080 12 12 20 40080
  //   22*12 80 32*12 100 2012 121 2012 12 12 800 12 10000 12 200 12 10000 12 10000 12 10000 12 12 12 20000
  //   12 10000 12 0 12 10000 12 12 0 12 10000 12
endmodule
